# Fritzing sketch MTE301_CircuitSchematic (saved by Fritzing 0.9.3b)
breadboards: 1

parts:
  Part1 = Arduino Mega ADK (Rev3)
  M1 = Stepper Motor - Bipolar
  M2 = Stepper Motor - Bipolar
  Part3 = EasyDriver_v44
  Part4 = EasyDriver_v44
  Part5 = Breadboard Power Supply Board SMD
  J1 = Basic Servo

nets:
  GND: Part1.GND, Part3.GND, Part4.GND, Part5.GND, J1.gnd
  N1: Part1.D2_PWM, Part4.STEP
  N2: Part1.D3_PWM, Part4.DIR
  N3: Part1.D4_PWM, Part3.DIR
  N4: Part1.D5_PWM, J1.pulse
  5V: Part1.5V, J1.vcc
  N5: Part1.D22, Part3.STEP
  N6: M1.A, Part4.OUT2A
  N7: M1.C, Part4.OUT2B
  N8: M1.B, Part4.OUT1B
  N9: M1.D, Part4.OUT1A
  N10: M2.A, Part3.OUT2B
  N11: M2.C, Part3.OUT2A
  N12: M2.B, Part3.OUT1B
  N13: M2.D, Part3.OUT1A
  N14: Part3.V+, Part4.V+, Part5.VCC

notes:
  Y AXIS
  X AXIS
  12 Volt Input
